// Logisim project beginner.circ as structural Verilog: 1 circuit, main circuit main
module main (
  input  in_1,
  input  in_2,
  output XOR_circuit
);

  wire and_1_out, and_2_out, not_1_out, not_2_out;

  not not_1 (not_1_out, in_1);
  and and_1 (and_1_out, not_1_out, in_2);
  and and_2 (and_2_out, in_1, not_2_out);
  not not_2 (not_2_out, in_2);
  or or_1 (XOR_circuit, and_1_out, and_2_out);
endmodule
