// Logisim project ram.circ as structural Verilog: 1 circuit, main circuit main
module main (
  input  Toggle_twice,
  input  in_2,
  input  in_3,
  input  READ_WRITE,
  input  in_5,
  input  DATA_INPUT,
  input  in_7,
  input  in_8,
  input  in_9,
  input  Toggle_twice_2,
  input  in_11
);

  wire and_1_out, and_2_out, and_3_out, and_4_out, and_5_out, and_6_out, and_7_out, and_8_out, and_9_out,
       and_10_out, and_11_out, and_12_out, and_13_out, and_14_out, and_15_out, and_16_out, and_17_out,
       and_18_out, and_19_out, and_20_out, and_21_out, and_22_out, and_23_out, and_24_out, and_25_out,
       and_26_out, and_27_out, and_28_out, and_29_out, and_30_out, and_31_out, and_32_out, and_33_out,
       j_k_ff_1_q, j_k_ff_1_qn, j_k_ff_2_q, j_k_ff_2_qn, j_k_ff_3_q, j_k_ff_3_qn, j_k_ff_4_q, j_k_ff_4_qn,
       j_k_ff_5_q, j_k_ff_5_qn, j_k_ff_6_q, j_k_ff_6_qn, j_k_ff_7_q, j_k_ff_7_qn, j_k_ff_8_q, j_k_ff_8_qn,
       j_k_ff_9_q, j_k_ff_9_qn, j_k_ff_10_q, j_k_ff_10_qn, j_k_ff_11_q, j_k_ff_11_qn, j_k_ff_12_q,
       j_k_ff_12_qn, j_k_ff_13_q, j_k_ff_13_qn, j_k_ff_14_q, j_k_ff_14_qn, j_k_ff_15_q, j_k_ff_15_qn,
       j_k_ff_16_q, j_k_ff_16_qn, j_k_ff_17_q, j_k_ff_17_qn, j_k_ff_18_q, j_k_ff_18_qn, j_k_ff_19_q,
       j_k_ff_19_qn, j_k_ff_20_q, j_k_ff_20_qn, j_k_ff_21_q, j_k_ff_21_qn, j_k_ff_22_q, j_k_ff_22_qn,
       j_k_ff_23_q, j_k_ff_23_qn, not_1_out, not_2_out, not_3_out, not_7_out, not_8_out, not_9_out,
       not_10_out, not_11_out, not_12_out, not_13_out, not_14_out, not_15_out, not_16_out, not_17_out,
       not_18_out, not_19_out, not_20_out, not_21_out, not_22_out, not_23_out, not_24_out, not_25_out,
       not_26_out, not_43_out, not_44_out, not_45_out, not_46_out, not_47_out, not_52_out, or_1_out,
       or_2_out, or_3_out, or_4_out, or_5_out, or_6_out, or_7_out, or_8_out, or_9_out;

  not not_1 (not_1_out, in_2);
  not not_2 (not_2_out, in_3);
  not not_3 (not_3_out, READ_WRITE);
  J_K_Flip_Flop j_k_ff_1 (
    .J(in_2), .clk(Toggle_twice), .K(not_1_out), .Q(j_k_ff_1_q), .Qn(j_k_ff_1_qn));  // open: preset, en, reset
  not not_4 (j_k_ff_1_q, j_k_ff_1_qn);
  J_K_Flip_Flop j_k_ff_2 (
    .J(in_3), .clk(Toggle_twice), .K(not_2_out), .Q(j_k_ff_2_q), .Qn(j_k_ff_2_qn));  // open: preset, en, reset
  not not_5 (j_k_ff_2_q, j_k_ff_2_qn);
  J_K_Flip_Flop j_k_ff_3 (
    .J(READ_WRITE), .clk(in_5), .K(not_3_out), .Q(j_k_ff_3_q), .Qn(j_k_ff_3_qn));  // open: preset, en, reset
  not not_6 (j_k_ff_3_q, j_k_ff_3_qn);
  not not_7 (not_7_out, j_k_ff_2_q);
  and and_1 (and_1_out, not_7_out, not_8_out);
  not not_8 (not_8_out, j_k_ff_1_q);
  and and_2 (and_2_out, j_k_ff_2_q, not_9_out);
  not not_9 (not_9_out, j_k_ff_1_q);
  not not_10 (not_10_out, j_k_ff_2_q);
  and and_3 (and_3_out, not_10_out, j_k_ff_1_q);
  and and_4 (and_4_out, j_k_ff_2_q, j_k_ff_1_q);
  and and_5 (and_5_out, and_1_out, j_k_ff_3_q);
  and and_6 (and_6_out, and_2_out, j_k_ff_3_q);
  and and_7 (and_7_out, and_3_out, j_k_ff_3_q);
  and and_8 (and_8_out, and_4_out, j_k_ff_3_q);
  not not_11 (not_11_out, and_29_out);
  not not_12 (not_12_out, and_28_out);
  not not_13 (not_13_out, and_27_out);
  not not_14 (not_14_out, and_26_out);
  not not_15 (not_15_out, and_29_out);
  not not_16 (not_16_out, and_28_out);
  not not_17 (not_17_out, and_27_out);
  not not_18 (not_18_out, and_26_out);
  not not_19 (not_19_out, and_29_out);
  not not_20 (not_20_out, and_28_out);
  not not_21 (not_21_out, and_27_out);
  not not_22 (not_22_out, and_26_out);
  not not_23 (not_23_out, and_29_out);
  not not_24 (not_24_out, and_28_out);
  not not_25 (not_25_out, and_27_out);
  not not_26 (not_26_out, and_26_out);
  J_K_Flip_Flop j_k_ff_4 (
    .clk(and_5_out), .K(not_11_out), .Q(j_k_ff_4_q), .Qn(j_k_ff_4_qn));  // open: J, preset, en, reset
  not not_27 (j_k_ff_4_q, j_k_ff_4_qn);
  J_K_Flip_Flop j_k_ff_5 (
    .clk(and_5_out), .K(not_12_out), .Q(j_k_ff_5_q), .Qn(j_k_ff_5_qn));  // open: J, preset, en, reset
  not not_28 (j_k_ff_5_q, j_k_ff_5_qn);
  J_K_Flip_Flop j_k_ff_6 (
    .clk(and_5_out), .K(not_13_out), .Q(j_k_ff_6_q), .Qn(j_k_ff_6_qn));  // open: J, preset, en, reset
  not not_29 (j_k_ff_6_q, j_k_ff_6_qn);
  J_K_Flip_Flop j_k_ff_7 (
    .clk(and_5_out), .K(not_14_out), .Q(j_k_ff_7_q), .Qn(j_k_ff_7_qn));  // open: J, preset, en, reset
  not not_30 (j_k_ff_7_q, j_k_ff_7_qn);
  J_K_Flip_Flop j_k_ff_8 (
    .J(and_29_out), .clk(and_6_out), .K(not_15_out), .Q(j_k_ff_8_q), .Qn(j_k_ff_8_qn));  // open: preset, en, reset
  not not_31 (j_k_ff_8_q, j_k_ff_8_qn);
  J_K_Flip_Flop j_k_ff_9 (
    .J(and_28_out), .clk(and_6_out), .K(not_16_out), .Q(j_k_ff_9_q), .Qn(j_k_ff_9_qn));  // open: preset, en, reset
  not not_32 (j_k_ff_9_q, j_k_ff_9_qn);
  J_K_Flip_Flop j_k_ff_10 (
    .J(and_27_out), .clk(and_6_out), .K(not_17_out), .Q(j_k_ff_10_q), .Qn(j_k_ff_10_qn));  // open: preset, en, reset
  not not_33 (j_k_ff_10_q, j_k_ff_10_qn);
  J_K_Flip_Flop j_k_ff_11 (
    .J(and_26_out), .clk(and_6_out), .K(not_18_out), .Q(j_k_ff_11_q), .Qn(j_k_ff_11_qn));  // open: preset, en, reset
  not not_34 (j_k_ff_11_q, j_k_ff_11_qn);
  J_K_Flip_Flop j_k_ff_12 (
    .J(and_29_out), .clk(and_7_out), .K(not_19_out), .Q(j_k_ff_12_q), .Qn(j_k_ff_12_qn));  // open: preset, en, reset
  not not_35 (j_k_ff_12_q, j_k_ff_12_qn);
  J_K_Flip_Flop j_k_ff_13 (
    .J(and_28_out), .clk(and_7_out), .K(not_20_out), .Q(j_k_ff_13_q), .Qn(j_k_ff_13_qn));  // open: preset, en, reset
  not not_36 (j_k_ff_13_q, j_k_ff_13_qn);
  J_K_Flip_Flop j_k_ff_14 (
    .J(and_27_out), .clk(and_7_out), .K(not_21_out), .Q(j_k_ff_14_q), .Qn(j_k_ff_14_qn));  // open: preset, en, reset
  not not_37 (j_k_ff_14_q, j_k_ff_14_qn);
  J_K_Flip_Flop j_k_ff_15 (
    .J(and_26_out), .clk(and_7_out), .K(not_22_out), .Q(j_k_ff_15_q), .Qn(j_k_ff_15_qn));  // open: preset, en, reset
  not not_38 (j_k_ff_15_q, j_k_ff_15_qn);
  J_K_Flip_Flop j_k_ff_16 (
    .J(and_29_out), .clk(and_8_out), .K(not_23_out), .Q(j_k_ff_16_q), .Qn(j_k_ff_16_qn));  // open: preset, en, reset
  not not_39 (j_k_ff_16_q, j_k_ff_16_qn);
  J_K_Flip_Flop j_k_ff_17 (
    .J(and_28_out), .clk(and_8_out), .K(not_24_out), .Q(j_k_ff_17_q), .Qn(j_k_ff_17_qn));  // open: preset, en, reset
  not not_40 (j_k_ff_17_q, j_k_ff_17_qn);
  J_K_Flip_Flop j_k_ff_18 (
    .J(and_27_out), .clk(and_8_out), .K(not_25_out), .Q(j_k_ff_18_q), .Qn(j_k_ff_18_qn));  // open: preset, en, reset
  not not_41 (j_k_ff_18_q, j_k_ff_18_qn);
  J_K_Flip_Flop j_k_ff_19 (
    .J(and_26_out), .clk(and_8_out), .K(not_26_out), .Q(j_k_ff_19_q), .Qn(j_k_ff_19_qn));  // open: preset, en, reset
  not not_42 (j_k_ff_19_q, j_k_ff_19_qn);
  not not_43 (not_43_out, j_k_ff_3_q);
  and and_9 (and_9_out, not_43_out, not_52_out);
  or or_1 (or_1_out, and_33_out, DATA_INPUT);
  or or_2 (or_2_out, and_32_out, in_7);
  or or_3 (or_3_out, and_31_out, in_8);
  or or_4 (or_4_out, and_30_out, in_9);
  and and_10 (and_10_out, and_1_out, not_43_out, j_k_ff_4_q);
  and and_11 (and_11_out, and_1_out, not_43_out, j_k_ff_5_q);
  and and_12 (and_12_out, and_1_out, not_43_out, j_k_ff_6_q);
  and and_13 (and_13_out, and_1_out, not_43_out, j_k_ff_7_q);
  and and_14 (and_14_out, and_2_out, not_43_out, j_k_ff_8_q);
  and and_15 (and_15_out, and_2_out, not_43_out, j_k_ff_9_q);
  and and_16 (and_16_out, and_2_out, not_43_out, j_k_ff_10_q);
  and and_17 (and_17_out, and_2_out, not_43_out, j_k_ff_11_q);
  and and_18 (and_18_out, and_3_out, not_43_out, j_k_ff_12_q);
  and and_19 (and_19_out, and_3_out, not_43_out, j_k_ff_13_q);
  and and_20 (and_20_out, and_3_out, not_43_out, j_k_ff_14_q);
  and and_21 (and_21_out, and_3_out, not_43_out, j_k_ff_15_q);
  and and_22 (and_22_out, and_4_out, not_43_out, j_k_ff_16_q);
  and and_23 (and_23_out, and_4_out, not_43_out, j_k_ff_17_q);
  and and_24 (and_24_out, and_4_out, not_43_out, j_k_ff_18_q);
  and and_25 (and_25_out, and_4_out, not_43_out, j_k_ff_19_q);
  not not_44 (not_44_out, or_1_out);
  not not_45 (not_45_out, or_2_out);
  not not_46 (not_46_out, or_3_out);
  not not_47 (not_47_out, or_4_out);
  or or_5 (or_5_out, and_9_out, Toggle_twice_2);
  or or_6 (or_6_out, and_10_out, and_14_out, and_18_out, and_22_out);
  J_K_Flip_Flop j_k_ff_20 (
    .J(or_1_out), .clk(or_5_out), .K(not_44_out), .Q(j_k_ff_20_q), .Qn(j_k_ff_20_qn));  // open: preset, en, reset
  not not_48 (j_k_ff_20_q, j_k_ff_20_qn);
  J_K_Flip_Flop j_k_ff_21 (
    .J(or_2_out), .clk(or_5_out), .K(not_45_out), .Q(j_k_ff_21_q), .Qn(j_k_ff_21_qn));  // open: preset, en, reset
  not not_49 (j_k_ff_21_q, j_k_ff_21_qn);
  J_K_Flip_Flop j_k_ff_22 (
    .J(or_3_out), .clk(or_5_out), .K(not_46_out), .Q(j_k_ff_22_q), .Qn(j_k_ff_22_qn));  // open: preset, en, reset
  not not_50 (j_k_ff_22_q, j_k_ff_22_qn);
  J_K_Flip_Flop j_k_ff_23 (
    .J(or_4_out), .clk(or_5_out), .K(not_47_out), .Q(j_k_ff_23_q), .Qn(j_k_ff_23_qn));  // open: preset, en, reset
  not not_51 (j_k_ff_23_q, j_k_ff_23_qn);
  or or_7 (or_7_out, and_11_out, and_15_out, and_19_out, and_23_out);
  or or_8 (or_8_out, and_12_out, and_16_out, and_20_out, and_24_out);
  and and_26 (and_26_out, not_52_out, j_k_ff_20_q);
  and and_27 (and_27_out, not_52_out, j_k_ff_21_q);
  and and_28 (and_28_out, not_52_out, j_k_ff_22_q);
  and and_29 (and_29_out, not_52_out, j_k_ff_23_q);
  not not_52 (not_52_out, Toggle_twice_2);
  or or_9 (or_9_out, and_13_out, and_17_out, and_21_out, and_25_out);
  and and_30 (and_30_out, or_6_out, not_43_out);
  and and_31 (and_31_out, or_7_out, not_43_out);
  and and_32 (and_32_out, or_8_out, not_43_out);
  and and_33 (and_33_out, or_9_out, not_43_out);

  // Notes on the sheet:
  //   Write to data register
  //   (Note: needs to be done after
  //   switching the RAM to read mode
  //   in order to write the stored nibble
  //   into the data register.)
  //   (Note #2: to write the DATA INPUT
  //   data into the data register,
  //   the RAM must be in write mode.)
  //   Write to address register
  //   Write to READ/WRITE register
  //   Toggle twice
  //   DATA REGISTER
endmodule
