// Logisim project adder.circ as structural Verilog: 1 circuit, main circuit main
module main (
  input  in_1,
  input  in_2,
  input  in_3,
  input  in_4,
  input  in_5,
  input  in_6,
  output out_7,
  output out_8,
  output out_9,
  output out_10
);

  wire and_1_out, and_2_out, and_3_out, and_4_out, and_5_out, clock_1_out, not_1_out, not_2_out, not_3_out,
       not_4_out, not_5_out, not_6_out, not_7_out, not_8_out, not_9_out, not_10_out, not_11_out, or_1_out,
       or_2_out, s_r_ff_1_q, s_r_ff_2_q, s_r_ff_3_q, s_r_ff_4_q, s_r_ff_5_q, s_r_ff_6_q, xor_1_out,
       xor_2_out, xor_3_out, xor_4_out, xor_5_out;

  Clock clock_1 (.out(clock_1_out));
  not not_1 (not_1_out, in_1);
  not not_2 (not_2_out, in_2);
  not not_3 (not_3_out, in_3);
  not not_4 (not_4_out, in_4);
  not not_5 (not_5_out, in_5);
  not not_6 (not_6_out, in_6);
  S_R_Flip_Flop s_r_ff_1 (.S(in_1), .clk(clock_1_out), .R(not_1_out), .Q(s_r_ff_1_q));  // open: Qn, preset, reset, en
  S_R_Flip_Flop s_r_ff_2 (.S(in_2), .clk(clock_1_out), .R(not_2_out), .Q(s_r_ff_2_q));  // open: Qn, preset, reset, en
  S_R_Flip_Flop s_r_ff_3 (.S(in_3), .clk(clock_1_out), .R(not_3_out), .Q(s_r_ff_3_q));  // open: Qn, preset, reset, en
  S_R_Flip_Flop s_r_ff_4 (.S(in_4), .clk(clock_1_out), .R(not_4_out), .Q(s_r_ff_4_q));  // open: Qn, preset, reset, en
  S_R_Flip_Flop s_r_ff_5 (.S(in_5), .clk(clock_1_out), .R(not_5_out), .Q(s_r_ff_5_q));  // open: Qn, preset, reset, en
  S_R_Flip_Flop s_r_ff_6 (.S(in_6), .clk(clock_1_out), .R(not_6_out), .Q(s_r_ff_6_q));  // open: Qn, preset, reset, en
  xor xor_1 (xor_1_out, s_r_ff_1_q, s_r_ff_4_q);
  and and_1 (and_1_out, s_r_ff_1_q, s_r_ff_4_q);
  xor xor_2 (xor_2_out, s_r_ff_2_q, s_r_ff_5_q);
  xor xor_3 (xor_3_out, s_r_ff_3_q, s_r_ff_6_q);
  xor xor_4 (xor_4_out, xor_2_out, and_1_out);
  and and_2 (and_2_out, xor_2_out, and_1_out);
  or or_1 (or_1_out, and_2_out, and_3_out);
  and and_3 (and_3_out, s_r_ff_2_q, s_r_ff_5_q);
  xor xor_5 (xor_5_out, xor_3_out, or_1_out);
  and and_4 (and_4_out, xor_3_out, or_1_out);
  or or_2 (or_2_out, and_4_out, and_5_out);
  and and_5 (and_5_out, s_r_ff_3_q, s_r_ff_6_q);
  not not_7 (not_7_out, clock_1_out);
  not not_8 (not_8_out, xor_1_out);
  not not_9 (not_9_out, xor_4_out);
  not not_10 (not_10_out, xor_5_out);
  not not_11 (not_11_out, or_2_out);
  S_R_Flip_Flop s_r_ff_7 (.S(xor_1_out), .clk(not_7_out), .R(not_8_out), .Q(out_7));  // open: Qn, preset, reset, en
  S_R_Flip_Flop s_r_ff_8 (.S(xor_4_out), .clk(not_7_out), .R(not_9_out), .Q(out_8));  // open: Qn, preset, reset, en
  S_R_Flip_Flop s_r_ff_9 (.S(xor_5_out), .clk(not_7_out), .R(not_10_out), .Q(out_9));  // open: Qn, preset, reset, en
  S_R_Flip_Flop s_r_ff_10 (.S(or_2_out), .clk(not_7_out), .R(not_11_out), .Q(out_10));  // open: Qn, preset, reset, en

  // Notes on the sheet:
  //   Operand 1
  //   2^0
  //   2^1
  //   2^2
  //   2^0
  //   2^1
  //   2^2
  //   Operand 2
  //   Half adder
  //   Full adder
  //   2^0 sum
  //   2^0 carry
  //   2^1 sum
  //   2^1 carry
  //   2^2 sum
  //   2^2 carry : overflow
endmodule
