// Logisim project 2s.circ as structural Verilog: 1 circuit, main circuit main
module main (
  input  _2_7,
  input  _2_6,
  input  _2_5,
  input  _2_4,
  input  _2_3,
  input  _2_2,
  input  _2_1,
  input  _2_0,
  input  in_9,
  output out_10,
  output out_11,
  output out_12,
  output out_13,
  output out_14,
  output out_15,
  output out_16,
  output out_17
);

  wire and_1_out, and_2_out, and_3_out, and_4_out, and_5_out, and_6_out, and_7_out, not_1_out, not_2_out,
       not_3_out, not_4_out, not_5_out, not_6_out, not_7_out, not_8_out;

  not not_1 (not_1_out, _2_7);
  not not_2 (not_2_out, _2_6);
  not not_3 (not_3_out, _2_5);
  not not_4 (not_4_out, _2_4);
  not not_5 (not_5_out, _2_3);
  not not_6 (not_6_out, _2_2);
  not not_7 (not_7_out, _2_1);
  not not_8 (not_8_out, _2_0);
  and and_1 (and_1_out, not_8_out, in_9);
  xor xor_1 (out_17, not_8_out, in_9);
  and and_2 (and_2_out, not_7_out, and_1_out);
  xor xor_2 (out_16, not_7_out, and_1_out);
  and and_3 (and_3_out, not_6_out, and_2_out);
  xor xor_3 (out_15, not_6_out, and_2_out);
  and and_4 (and_4_out, not_5_out, and_3_out);
  xor xor_4 (out_14, not_5_out, and_3_out);
  and and_5 (and_5_out, not_4_out, and_4_out);
  xor xor_5 (out_13, not_4_out, and_4_out);
  and and_6 (and_6_out, not_3_out, and_5_out);
  xor xor_6 (out_12, not_3_out, and_5_out);
  and and_7 (and_7_out, not_2_out, and_6_out);
  xor xor_7 (out_11, not_2_out, and_6_out);
  xor xor_8 (out_10, not_1_out, and_7_out);
endmodule
