// Logisim project 2to10.circ as structural Verilog: 1 circuit, main circuit main
module main (
  input  _2_7,
  input  _2_6,
  input  _2_5,
  input  _2_4,
  input  _2_3,
  input  _2_2,
  input  _2_1,
  input  _2_0,
  output _10_2_2_1,
  output _10_2_2_0,
  output _10_1_2_3,
  output _10_1_2_2,
  output _10_1_2_1,
  output _10_1_2_0,
  output _10_0_2_3,
  output _10_0_2_2,
  output _10_0_2_1,
  output _10_0_2_0
);

  wire add3_1__2_0_2, add3_1__2_1_2, add3_1__2_2_2, add3_1__2_3_2, add3_2__2_0_2, add3_2__2_1_2,
       add3_2__2_2_2, add3_2__2_3_2, add3_3__2_0_2, add3_3__2_1_2, add3_3__2_2_2, add3_3__2_3_2,
       add3_4__2_0_2, add3_4__2_1_2, add3_4__2_2_2, add3_6__2_0_2, add3_6__2_1_2, add3_6__2_2_2,
       add3_6__2_3_2, and_1_out, not_1_out;

  not not_1 (not_1_out, _2_7);
  and and_1 (and_1_out, not_1_out, _2_7);
  Add3 add3_1 (
    ._2_3(and_1_out), ._2_2(_2_7), ._2_1(_2_6), ._2_0(_2_5), ._2_3_2(add3_1__2_3_2), ._2_2_2(add3_1__2_2_2),
    ._2_1_2(add3_1__2_1_2), ._2_0_2(add3_1__2_0_2));  // open: ERROR
  Add3 add3_2 (
    ._2_3(add3_1__2_2_2), ._2_2(add3_1__2_1_2), ._2_1(add3_1__2_0_2), ._2_0(_2_4), ._2_3_2(add3_2__2_3_2),
    ._2_2_2(add3_2__2_2_2), ._2_1_2(add3_2__2_1_2), ._2_0_2(add3_2__2_0_2));  // open: ERROR
  Add3 add3_3 (
    ._2_3(add3_2__2_2_2), ._2_2(add3_2__2_1_2), ._2_1(add3_2__2_0_2), ._2_0(_2_3), ._2_3_2(add3_3__2_3_2),
    ._2_2_2(add3_3__2_2_2), ._2_1_2(add3_3__2_1_2), ._2_0_2(add3_3__2_0_2));  // open: ERROR
  Add3 add3_4 (
    ._2_3(and_1_out), ._2_2(add3_1__2_3_2), ._2_1(add3_2__2_3_2), ._2_0(add3_3__2_3_2), ._2_3_2(_10_2_2_1),
    ._2_2_2(add3_4__2_2_2), ._2_1_2(add3_4__2_1_2), ._2_0_2(add3_4__2_0_2));  // open: ERROR
  Add3 add3_5 (
    ._2_3(add3_4__2_2_2), ._2_2(add3_4__2_1_2), ._2_1(add3_4__2_0_2), ._2_0(add3_6__2_3_2),
    ._2_3_2(_10_2_2_0), ._2_2_2(_10_1_2_3), ._2_1_2(_10_1_2_2), ._2_0_2(_10_1_2_1));  // open: ERROR
  Add3 add3_6 (
    ._2_3(add3_3__2_2_2), ._2_2(add3_3__2_1_2), ._2_1(add3_3__2_0_2), ._2_0(_2_2), ._2_3_2(add3_6__2_3_2),
    ._2_2_2(add3_6__2_2_2), ._2_1_2(add3_6__2_1_2), ._2_0_2(add3_6__2_0_2));  // open: ERROR
  Add3 add3_7 (
    ._2_3(add3_6__2_2_2), ._2_2(add3_6__2_1_2), ._2_1(add3_6__2_0_2), ._2_0(_2_1), ._2_3_2(_10_1_2_0),
    ._2_2_2(_10_0_2_3), ._2_1_2(_10_0_2_2), ._2_0_2(_10_0_2_1));  // open: ERROR
  // display_decoder_main main_1: pin names not known
  // display_decoder_main main_2: pin names not known
  // display_decoder_main main_3: pin names not known

  assign _10_0_2_0 = _2_0;
endmodule
