// Logisim project MBR.circ as structural Verilog: 1 circuit, main circuit main
module main (
  input  in_1,
  input  in_2,
  input  in_3,
  input  in_4,
  input  in_5,
  input  in_6,
  input  in_7,
  input  in_8,
  input  in_9
);

  wire and_1_out, and_2_out, and_3_out, and_4_out, and_5_out, and_6_out, and_7_out, and_8_out, not_1_out,
       not_2_out, not_3_out, not_4_out, not_5_out, not_6_out, not_7_out, not_8_out, s_r_ff_1_q, s_r_ff_2_q,
       s_r_ff_3_q, s_r_ff_4_q, s_r_ff_5_q, s_r_ff_6_q, s_r_ff_7_q, s_r_ff_8_q;

  S_R_Flip_Flop s_r_ff_1 (.S(not_1_out), .R(in_2), .Q(s_r_ff_1_q));  // open: clk, Qn, preset, reset, en
  not not_1 (not_1_out, in_2);
  S_R_Flip_Flop s_r_ff_2 (.S(not_2_out), .R(in_3), .Q(s_r_ff_2_q));  // open: clk, Qn, preset, reset, en
  not not_2 (not_2_out, in_3);
  not not_3 (not_3_out, in_4);
  S_R_Flip_Flop s_r_ff_3 (.S(not_3_out), .R(in_4), .Q(s_r_ff_3_q));  // open: clk, Qn, preset, reset, en
  not not_4 (not_4_out, in_5);
  S_R_Flip_Flop s_r_ff_4 (.S(not_4_out), .R(in_5), .Q(s_r_ff_4_q));  // open: clk, Qn, preset, reset, en
  S_R_Flip_Flop s_r_ff_5 (.S(not_5_out), .R(in_6), .Q(s_r_ff_5_q));  // open: clk, Qn, preset, reset, en
  not not_5 (not_5_out, in_6);
  S_R_Flip_Flop s_r_ff_6 (.S(not_6_out), .R(in_7), .Q(s_r_ff_6_q));  // open: clk, Qn, preset, reset, en
  not not_6 (not_6_out, in_7);
  not not_7 (not_7_out, in_8);
  S_R_Flip_Flop s_r_ff_7 (.S(not_7_out), .R(in_8), .Q(s_r_ff_7_q));  // open: clk, Qn, preset, reset, en
  S_R_Flip_Flop s_r_ff_8 (.S(not_8_out), .R(in_9), .Q(s_r_ff_8_q));  // open: clk, Qn, preset, reset, en
  not not_8 (not_8_out, in_9);
  and and_1 (and_1_out, in_1, s_r_ff_1_q);
  and and_2 (and_2_out, s_r_ff_2_q, in_1);
  and and_3 (and_3_out, s_r_ff_3_q, in_1);
  and and_4 (and_4_out, s_r_ff_4_q, in_1);
  and and_5 (and_5_out, s_r_ff_5_q, in_1);
  and and_6 (and_6_out, s_r_ff_6_q, in_1);
  and and_7 (and_7_out, s_r_ff_7_q, in_1);
  and and_8 (and_8_out, s_r_ff_8_q, in_1);

  // Notes on the sheet:
  //   CU
endmodule
