// Logisim project alu.circ as structural Verilog: 1 circuit, main circuit main
module main (
  input  _2_7,
  input  _2_6,
  input  _2_5_prime,
  input  _2_4,
  input  _2_3,
  input  _2_2,
  input  _2_1,
  input  _2_0,
  input  in_9,
  input  SUBTRACT_MODE,
  input  _2_7_2,
  input  _2_6_2,
  input  _2_5_prime_2,
  input  _2_4_2,
  input  _2_3_2,
  input  _2_2_2,
  input  _2_1_2,
  input  _2_0_2,
  input  in_19
);

  wire _2_0_2_out, _2_0_out, _2_1_2_out, _2_1_out, _2_2_2_out, _2_2_out, _2_3_2_out, _2_3_out, _2_4_2_out,
       _2_4_out, _2_5_2_out, _2_5_out, _2_6_2_out, _2_6_out, _2_7_2_out, _2_7_out, and_1_out, and_2_out,
       and_3_out, and_4_out, and_5_out, and_6_out, and_7_out, and_8_out, and_9_out, and_10_out, and_11_out,
       and_12_out, and_13_out, and_14_out, and_15_out, and_16_out, and_17_out, and_18_out, and_19_out,
       and_20_out, and_21_out, and_22_out, and_23_out, and_24_out, and_25_out, and_26_out, and_27_out,
       and_28_out, and_29_out, and_30_out, and_31_out, and_32_out, and_33_out, and_34_out, and_35_out,
       and_36_out, and_37_out, and_38_out, and_39_out, and_40_out, and_41_out, and_42_out, and_43_out,
       and_44_out, and_45_out, and_46_out, not_1_out, not_2_out, not_3_out, not_4_out, not_5_out, not_6_out,
       not_7_out, not_8_out, not_9_out, not_10_out, or_1_out, or_2_out, or_3_out, or_4_out, or_5_out,
       or_6_out, or_7_out, OVERFLOW_out, xor_1_out, xor_2_out, xor_3_out, xor_4_out, xor_5_out, xor_6_out,
       xor_7_out, xor_8_out, xor_9_out, xor_10_out, xor_11_out, xor_12_out, xor_13_out, xor_14_out,
       xor_15_out;

  xor u__2_0 (_2_0_out, _2_0, _2_0_2_out);
  and and_1 (and_1_out, _2_0, _2_0_2_out);
  xor xor_1 (xor_1_out, _2_3, _2_3_2_out);
  xor xor_2 (xor_2_out, _2_4, _2_4_2_out);
  xor xor_3 (xor_3_out, _2_5_prime, _2_5_2_out);
  xor xor_4 (xor_4_out, _2_6, _2_6_2_out);
  xor xor_5 (xor_5_out, _2_7, _2_7_out);
  or u__2_7 (_2_7_out, and_9_out, and_31_out);
  and and_2 (and_2_out, _2_0_2, not_1_out);
  and and_3 (and_3_out, _2_1_2, not_1_out);
  and and_4 (and_4_out, _2_2_2, not_1_out);
  and and_5 (and_5_out, _2_3_2, not_1_out);
  and and_6 (and_6_out, _2_4_2, not_1_out);
  and and_7 (and_7_out, _2_5_prime_2, not_1_out);
  and and_8 (and_8_out, _2_6_2, not_1_out);
  and and_9 (and_9_out, _2_7_2, not_1_out);
  xor xor_6 (xor_6_out, _2_1, _2_1_2_out);
  and and_10 (and_10_out, xor_6_out, and_1_out);
  and and_11 (and_11_out, _2_1, _2_1_2_out);
  xor xor_7 (xor_7_out, _2_2, _2_2_2_out);
  and and_12 (and_12_out, xor_7_out, or_1_out);
  and and_13 (and_13_out, _2_2, _2_2_2_out);
  xor u__2_3 (_2_3_out, xor_1_out, or_2_out);
  and and_14 (and_14_out, xor_1_out, or_2_out);
  and and_15 (and_15_out, _2_3, _2_3_2_out);
  xor u__2_4 (_2_4_out, xor_2_out, or_3_out);
  and and_16 (and_16_out, xor_2_out, or_3_out);
  and and_17 (and_17_out, _2_4, _2_4_2_out);
  xor _2_5 (_2_5_out, xor_3_out, or_4_out);
  and and_18 (and_18_out, xor_3_out, or_4_out);
  and and_19 (and_19_out, _2_5_prime, _2_5_2_out);
  xor u__2_6 (_2_6_out, xor_4_out, or_5_out);
  and and_20 (and_20_out, xor_4_out, or_5_out);
  and and_21 (and_21_out, _2_6, _2_6_2_out);
  xor u__2_7_2 (_2_7_2_out, xor_5_out, or_6_out);
  and and_22 (and_22_out, xor_5_out, or_6_out);
  and and_23 (and_23_out, _2_7, _2_7_out);
  or _2_5_2 (_2_5_2_out, and_7_out, and_29_out);
  or u__2_6_2 (_2_6_2_out, and_8_out, and_30_out);
  xor u__2_1 (_2_1_out, xor_6_out, and_1_out);
  or or_1 (or_1_out, and_10_out, and_11_out);
  xor u__2_2 (_2_2_out, xor_7_out, or_1_out);
  or or_2 (or_2_out, and_12_out, and_13_out);
  or or_3 (or_3_out, and_14_out, and_15_out);
  or or_4 (or_4_out, and_16_out, and_17_out);
  or or_5 (or_5_out, and_18_out, and_19_out);
  or or_6 (or_6_out, and_20_out, and_21_out);
  or or_7 (or_7_out, and_22_out, and_23_out);
  or u__2_3_2 (_2_3_2_out, and_5_out, and_27_out);
  or u__2_4_2 (_2_4_2_out, and_6_out, and_28_out);
  or u__2_2_2 (_2_2_2_out, and_4_out, and_26_out);
  or u__2_1_2 (_2_1_2_out, and_3_out, and_25_out);
  not not_1 (not_1_out, SUBTRACT_MODE);
  or u__2_0_2 (_2_0_2_out, and_2_out, and_24_out);
  and and_24 (and_24_out, xor_8_out, SUBTRACT_MODE);
  and and_25 (and_25_out, xor_9_out, SUBTRACT_MODE);
  and and_26 (and_26_out, xor_10_out, SUBTRACT_MODE);
  and and_27 (and_27_out, xor_11_out, SUBTRACT_MODE);
  and and_28 (and_28_out, xor_12_out, SUBTRACT_MODE);
  and and_29 (and_29_out, xor_14_out, SUBTRACT_MODE);
  and and_30 (and_30_out, xor_13_out, SUBTRACT_MODE);
  and and_31 (and_31_out, xor_15_out, SUBTRACT_MODE);
  xor OVERFLOW (OVERFLOW_out, or_6_out, or_7_out);
  and and_32 (and_32_out, SUBTRACT_MODE, _2_7_2);
  not not_2 (not_2_out, and_32_out);
  and and_33 (and_33_out, SUBTRACT_MODE, _2_6_2);
  not not_3 (not_3_out, and_33_out);
  not not_4 (not_4_out, and_34_out);
  and and_34 (and_34_out, SUBTRACT_MODE, _2_5_prime_2);
  and and_35 (and_35_out, SUBTRACT_MODE, _2_4_2);
  not not_5 (not_5_out, and_35_out);
  and and_36 (and_36_out, SUBTRACT_MODE, _2_3_2);
  not not_6 (not_6_out, and_36_out);
  not not_7 (not_7_out, and_37_out);
  and and_37 (and_37_out, SUBTRACT_MODE, _2_2_2);
  not not_8 (not_8_out, and_38_out);
  and and_38 (and_38_out, SUBTRACT_MODE, _2_1_2);
  and and_39 (and_39_out, SUBTRACT_MODE, _2_0_2);
  not not_9 (not_9_out, and_39_out);
  not not_10 (not_10_out, in_9);
  and and_40 (and_40_out, not_9_out, not_10_out);
  xor xor_8 (xor_8_out, not_9_out, not_10_out);
  and and_41 (and_41_out, not_8_out, and_40_out);
  xor xor_9 (xor_9_out, not_8_out, and_40_out);
  and and_42 (and_42_out, not_7_out, and_41_out);
  xor xor_10 (xor_10_out, not_7_out, and_41_out);
  and and_43 (and_43_out, not_6_out, and_42_out);
  xor xor_11 (xor_11_out, not_6_out, and_42_out);
  and and_44 (and_44_out, not_5_out, and_43_out);
  xor xor_12 (xor_12_out, not_5_out, and_43_out);
  and and_45 (and_45_out, not_4_out, and_44_out);
  and and_46 (and_46_out, not_3_out, and_45_out);
  xor xor_13 (xor_13_out, not_3_out, and_45_out);
  xor xor_14 (xor_14_out, not_4_out, and_44_out);
  xor xor_15 (xor_15_out, not_2_out, and_46_out);

  // Notes on the sheet:
  //   2^7
  //   2^6
  //   2^5
  //   2^4
  //   2^3
  //   2^2
  //   2^1
  //   2^0
endmodule
