// Logisim project cu.circ as structural Verilog: 1 circuit, main circuit main
module main (
  input  in_1
);

  wire and_1_out, and_2_out, and_3_out, and_4_out, and_5_out, and_6_out, and_7_out, and_8_out, and_9_out,
       clock_1_out, j_k_ff_1_q, j_k_ff_2_q, j_k_ff_3_q, j_k_ff_4_q, j_k_ff_5_q, j_k_ff_6_q, j_k_ff_7_q,
       j_k_ff_8_q, j_k_ff_9_q, not_1_out, not_2_out, not_3_out, not_4_out, not_5_out, not_6_out, not_7_out,
       not_8_out, not_9_out, not_10_out, not_11_out, not_12_out, not_13_out, not_14_out, not_15_out,
       not_16_out, not_17_out, not_18_out, not_19_out, not_20_out, not_21_out, not_22_out, not_23_out,
       not_24_out, not_25_out, not_26_out, not_27_out, not_28_out, not_29_out, not_30_out, or_1_out, or_2_out;

  Clock clock_1 (.out(clock_1_out));
  not not_1 (not_1_out, j_k_ff_2_q);
  not not_2 (not_2_out, j_k_ff_5_q);
  not not_3 (not_3_out, j_k_ff_8_q);
  not not_4 (not_4_out, j_k_ff_9_q);
  not not_5 (not_5_out, j_k_ff_6_q);
  and and_1 (and_1_out, not_1_out, not_2_out, not_3_out, not_4_out);
  and and_2 (and_2_out, and_1_out, clock_1_out);
  and and_3 (and_3_out, not_5_out, in_1);
  J_K_Flip_Flop j_k_ff_1 (
    .J(and_3_out), .clk(clock_1_out), .K(not_6_out), .Q(j_k_ff_1_q));  // open: Qn, preset, en, reset
  not not_6 (not_6_out, and_3_out);
  or or_1 (or_1_out, and_1_out, and_4_out);
  or or_2 (or_2_out, and_2_out, and_7_out);
  not not_7 (not_7_out, or_1_out);
  not not_8 (not_8_out, j_k_ff_1_q);
  and and_4 (and_4_out, j_k_ff_9_q, not_9_out, not_10_out, not_11_out);
  J_K_Flip_Flop j_k_ff_2 (.J(or_1_out), .clk(or_2_out), .K(not_7_out), .Q(j_k_ff_2_q));  // open: Qn, preset, en, reset
  J_K_Flip_Flop j_k_ff_3 (
    .J(j_k_ff_1_q), .clk(clock_1_out), .K(not_8_out), .Q(j_k_ff_3_q));  // open: Qn, preset, en, reset
  not not_9 (not_9_out, j_k_ff_8_q);
  not not_10 (not_10_out, j_k_ff_5_q);
  not not_11 (not_11_out, j_k_ff_2_q);
  not not_12 (not_12_out, and_5_out);
  J_K_Flip_Flop j_k_ff_4 (
    .J(j_k_ff_3_q), .clk(clock_1_out), .K(not_13_out), .Q(j_k_ff_4_q));  // open: Qn, preset, en, reset
  not not_13 (not_13_out, j_k_ff_3_q);
  and and_5 (and_5_out, j_k_ff_2_q, not_15_out, not_16_out, not_17_out);
  J_K_Flip_Flop j_k_ff_5 (
    .J(and_5_out), .clk(and_7_out), .K(not_12_out), .Q(j_k_ff_5_q));  // open: Qn, preset, en, reset
  not not_14 (not_14_out, j_k_ff_4_q);
  not not_15 (not_15_out, j_k_ff_5_q);
  not not_16 (not_16_out, j_k_ff_8_q);
  not not_17 (not_17_out, j_k_ff_9_q);
  J_K_Flip_Flop j_k_ff_6 (
    .J(j_k_ff_4_q), .clk(clock_1_out), .K(not_14_out), .Q(j_k_ff_6_q));  // open: Qn, preset, en, reset
  not not_18 (not_18_out, and_6_out);
  J_K_Flip_Flop j_k_ff_7 (
    .J(j_k_ff_6_q), .clk(clock_1_out), .K(not_19_out), .Q(j_k_ff_7_q));  // open: Qn, preset, en, reset
  not not_19 (not_19_out, j_k_ff_6_q);
  not not_20 (not_20_out, j_k_ff_8_q);
  not not_21 (not_21_out, j_k_ff_9_q);
  and and_6 (and_6_out, j_k_ff_5_q, not_20_out, not_21_out, not_22_out);
  not not_22 (not_22_out, j_k_ff_2_q);
  J_K_Flip_Flop j_k_ff_8 (
    .J(and_6_out), .clk(and_7_out), .K(not_18_out), .Q(j_k_ff_8_q));  // open: Qn, preset, en, reset
  and and_7 (and_7_out, j_k_ff_7_q, and_8_out);
  not not_23 (not_23_out, j_k_ff_3_q);
  not not_24 (not_24_out, j_k_ff_6_q);
  and and_8 (and_8_out, not_23_out, not_24_out, not_25_out, not_26_out);
  not not_25 (not_25_out, j_k_ff_4_q);
  not not_26 (not_26_out, j_k_ff_1_q);
  J_K_Flip_Flop j_k_ff_9 (
    .J(and_9_out), .clk(and_7_out), .K(not_27_out), .Q(j_k_ff_9_q));  // open: Qn, preset, en, reset
  not not_27 (not_27_out, and_9_out);
  not not_28 (not_28_out, j_k_ff_2_q);
  and and_9 (and_9_out, j_k_ff_8_q, not_28_out, not_29_out, not_30_out);
  not not_29 (not_29_out, j_k_ff_5_q);
  not not_30 (not_30_out, j_k_ff_9_q);

  // Notes on the sheet:
  //   MASTER CONTROL UNIT
endmodule
