// Logisim project display-decoder.circ as structural Verilog: 1 circuit, main circuit main
module main (
  input  _2_3,
  input  _2_2,
  input  _2_1,
  input  _2_0,
  output Top_1,
  output Top_2,
  output Top_3,
  output Top_4,
  output Bottom_1,
  output Bottom_2,
  output Bottom_3,
  output Bottom_4,
  output ERROR
);

  wire and_1_out, and_2_out, and_3_out, and_4_out, and_5_out, and_6_out, and_7_out, and_8_out, and_9_out,
       and_10_out, not_1_out, not_2_out, not_3_out, not_4_out, not_5_out, not_6_out, not_7_out, not_8_out,
       not_9_out, not_10_out, not_11_out, not_12_out, not_13_out, not_14_out, not_15_out, not_16_out,
       not_17_out, not_18_out, not_19_out, not_20_out, not_21_out, not_22_out, not_23_out, not_24_out,
       not_25_out, not_26_out, not_27_out, not_28_out, not_29_out, not_30_out, not_31_out, not_32_out,
       not_33_out, not_34_out, not_35_out, not_36_out;

  not not_1 (not_1_out, _2_2);
  and and_1 (and_1_out, _2_3, not_1_out, not_2_out, _2_0);
  not not_2 (not_2_out, _2_1);
  not not_3 (not_3_out, _2_2);
  and and_2 (and_2_out, _2_3, not_3_out, not_4_out, not_5_out);
  not not_4 (not_4_out, _2_1);
  not not_5 (not_5_out, _2_0);
  not not_6 (not_6_out, _2_3);
  and and_3 (and_3_out, not_6_out, _2_2, _2_1, _2_0);
  not not_7 (not_7_out, _2_3);
  and and_4 (and_4_out, not_7_out, _2_2, _2_1, not_8_out);
  not not_8 (not_8_out, _2_0);
  not not_9 (not_9_out, _2_3);
  and and_5 (and_5_out, not_9_out, _2_2, not_10_out, _2_0);
  not not_10 (not_10_out, _2_1);
  not not_11 (not_11_out, _2_3);
  and and_6 (and_6_out, not_11_out, _2_2, not_12_out, not_13_out);
  not not_12 (not_12_out, _2_1);
  not not_13 (not_13_out, _2_0);
  not not_14 (not_14_out, _2_3);
  not not_15 (not_15_out, _2_2);
  and and_7 (and_7_out, not_14_out, not_15_out, _2_1, _2_0);
  not not_16 (not_16_out, _2_3);
  not not_17 (not_17_out, _2_2);
  and and_8 (and_8_out, not_16_out, not_17_out, _2_1, not_18_out);
  not not_18 (not_18_out, _2_0);
  not not_19 (not_19_out, _2_3);
  not not_20 (not_20_out, _2_2);
  and and_9 (and_9_out, not_19_out, not_20_out, not_21_out, _2_0);
  not not_21 (not_21_out, _2_1);
  not not_22 (not_22_out, _2_3);
  not not_23 (not_23_out, _2_2);
  and and_10 (and_10_out, not_22_out, not_23_out, not_24_out, not_25_out);
  not not_24 (not_24_out, _2_1);
  not not_25 (not_25_out, _2_0);
  or or_1 (Top_4, and_1_out, and_2_out, and_3_out, and_6_out, and_7_out, and_8_out, and_9_out, and_10_out);
  or or_2 (Top_3, and_1_out, and_2_out, and_3_out, and_5_out, and_7_out, and_8_out, and_10_out);
  or or_3 (Top_2, and_1_out, and_2_out, and_4_out, and_5_out, and_6_out, and_10_out);
  or or_4 (Top_1, and_1_out, and_2_out, and_4_out, and_5_out, and_6_out, and_7_out, and_8_out);
  _7_Segment_Display u_7_segment_display_1 (
    .g(Top_1), .f(Top_2), .a(Top_3), .b(Top_4), .e(Bottom_1), .d(Bottom_2), .c(Bottom_3), .dp(Bottom_4));
  or or_5 (Bottom_1, and_2_out, and_4_out, and_8_out, and_10_out);
  or or_6 (Bottom_2, and_2_out, and_4_out, and_5_out, and_7_out, and_8_out, and_10_out);
  or or_7 (Bottom_3, and_1_out, and_2_out, and_3_out, and_4_out, and_5_out, and_6_out, and_7_out, and_9_out, and_10_out);
  not not_26 (not_26_out, and_10_out);
  and and_11 (Bottom_4, not_26_out, and_10_out);
  not not_27 (not_27_out, and_10_out);
  not not_28 (not_28_out, and_9_out);
  not not_29 (not_29_out, and_8_out);
  not not_30 (not_30_out, and_7_out);
  not not_31 (not_31_out, and_6_out);
  not not_32 (not_32_out, and_5_out);
  not not_33 (not_33_out, and_4_out);
  not not_34 (not_34_out, and_3_out);
  not not_35 (not_35_out, and_2_out);
  not not_36 (not_36_out, and_1_out);
  and and_12 (ERROR, not_27_out, not_28_out, not_29_out, not_30_out, not_31_out, not_32_out, not_33_out, not_34_out, not_35_out, not_36_out);

  // Notes on the sheet:
  //   the dot is always off
endmodule
