// Logisim project display.circ as structural Verilog: 1 circuit, main circuit main
module main (
  input  in_1,
  input  in_2,
  input  in_3,
  input  in_4,
  input  in_5,
  input  in_6,
  input  in_7,
  input  in_8
);

  wire and_1_out, main_1__10_0_2_0, main_1__10_0_2_1, main_1__10_0_2_2, main_1__10_0_2_3, main_1__10_1_2_0,
       main_1__10_1_2_1, main_1__10_1_2_2, main_1__10_1_2_3, main_1__10_2_2_0, main_1__10_2_2_1,
       main_2_bottom_1, main_2_bottom_2, main_2_bottom_3, main_2_bottom_4, main_2_top_1, main_2_top_2,
       main_2_top_3, main_2_top_4, main_3_bottom_1, main_3_bottom_2, main_3_bottom_3, main_3_bottom_4,
       main_3_top_1, main_3_top_2, main_3_top_3, main_3_top_4, main_4_bottom_1, main_4_bottom_2,
       main_4_bottom_3, main_4_bottom_4, main_4_top_1, main_4_top_2, main_4_top_3, main_4_top_4, not_1_out;

  _2to10_main main_1 (
    ._2_7(in_1), ._2_6(in_2), ._2_5(in_3), ._2_4(in_4), ._2_3(in_5), ._2_2(in_6), ._2_1(in_7), ._2_0(in_8),
    ._10_2_2_1(main_1__10_2_2_1), ._10_2_2_0(main_1__10_2_2_0), ._10_1_2_3(main_1__10_1_2_3),
    ._10_1_2_2(main_1__10_1_2_2), ._10_1_2_1(main_1__10_1_2_1), ._10_1_2_0(main_1__10_1_2_0),
    ._10_0_2_3(main_1__10_0_2_3), ._10_0_2_2(main_1__10_0_2_2), ._10_0_2_1(main_1__10_0_2_1),
    ._10_0_2_0(main_1__10_0_2_0));
  not not_1 (not_1_out, main_1__10_2_2_1);
  and and_1 (and_1_out, not_1_out, main_1__10_2_2_1);
  display_decoder_main main_2 (
    ._2_3(and_1_out), ._2_2(and_1_out), ._2_1(main_1__10_2_2_1), ._2_0(main_1__10_2_2_0),
    .Top_1(main_2_top_1), .Top_2(main_2_top_2), .Top_3(main_2_top_3), .Top_4(main_2_top_4),
    .Bottom_1(main_2_bottom_1), .Bottom_2(main_2_bottom_2), .Bottom_3(main_2_bottom_3),
    .Bottom_4(main_2_bottom_4));  // open: ERROR
  display_decoder_main main_3 (
    ._2_3(main_1__10_1_2_3), ._2_2(main_1__10_1_2_2), ._2_1(main_1__10_1_2_1), ._2_0(main_1__10_1_2_0),
    .Top_1(main_3_top_1), .Top_2(main_3_top_2), .Top_3(main_3_top_3), .Top_4(main_3_top_4),
    .Bottom_1(main_3_bottom_1), .Bottom_2(main_3_bottom_2), .Bottom_3(main_3_bottom_3),
    .Bottom_4(main_3_bottom_4));  // open: ERROR
  display_decoder_main main_4 (
    ._2_3(main_1__10_0_2_3), ._2_2(main_1__10_0_2_2), ._2_1(main_1__10_0_2_1), ._2_0(main_1__10_0_2_0),
    .Top_1(main_4_top_1), .Top_2(main_4_top_2), .Top_3(main_4_top_3), .Top_4(main_4_top_4),
    .Bottom_1(main_4_bottom_1), .Bottom_2(main_4_bottom_2), .Bottom_3(main_4_bottom_3),
    .Bottom_4(main_4_bottom_4));  // open: ERROR
  _7_Segment_Display u_7_segment_display_1 (
    .g(main_3_top_1), .f(main_3_top_2), .a(main_3_top_3), .b(main_3_top_4), .e(main_3_bottom_1),
    .d(main_3_bottom_2), .c(main_3_bottom_3), .dp(main_3_bottom_4));
  _7_Segment_Display u_7_segment_display_2 (
    .g(main_2_top_1), .f(main_2_top_2), .a(main_2_top_3), .b(main_2_top_4), .e(main_2_bottom_1),
    .d(main_2_bottom_2), .c(main_2_bottom_3), .dp(main_2_bottom_4));
  _7_Segment_Display u_7_segment_display_3 (
    .g(main_4_top_1), .f(main_4_top_2), .a(main_4_top_3), .b(main_4_top_4), .e(main_4_bottom_1),
    .d(main_4_bottom_2), .c(main_4_bottom_3), .dp(main_4_bottom_4));

  // Notes on the sheet:
  //   Copy-paste into main circuit
endmodule
